# Fritzing sketch board (saved by Fritzing 1.0.3b)
breadboards: 1

parts:
  Pico/Pico2_Mod_1 = Raspberry Pi Pico or Pico 2
  HC-SR04_Sensor_1 = HC-SR04 Ultrasonic Distance Sensor
  Part2 = GY-VL53L0XV2 Laser Ranger Module

nets:
  GND: Pico/Pico2_Mod_1.pin_3, Pico/Pico2_Mod_1.pin_8, Pico/Pico2_Mod_1.pin_13, Pico/Pico2_Mod_1.pin_18, Pico/Pico2_Mod_1.pin_23, Pico/Pico2_Mod_1.pin_28, Pico/Pico2_Mod_1.pin_33, Pico/Pico2_Mod_1.pin_38, HC-SR04_Sensor_1.GND, Part2.GND
  N1: Pico/Pico2_Mod_1.pin_21, Pico/Pico2_Mod_1.pin_43, HC-SR04_Sensor_1.TRIG
  N2: Pico/Pico2_Mod_1.pin_22, HC-SR04_Sensor_1.ECHO
  N3: Pico/Pico2_Mod_1.pin_26, Part2.SDA
  N4: Pico/Pico2_Mod_1.pin_27, Part2.SCL
  VCC: Pico/Pico2_Mod_1.pin_36, HC-SR04_Sensor_1.VCC, Part2.VCC

custom parts:
  Raspberry Pi Pico or Pico 2: Raspberry Pi Pico and Pico 2. Based around the RP2040 and RP2350 microcontrollers respectively, Picos are low cost microcontroller device bringing Raspberry Pi quality, cost, and easy of use to the microcontroller space. Jan 2021, Split part in to two versions: tht (this one) and SMD. This one will drill holes for a .1 in header in pcb to allow plugging in the module as well as providing pads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
  GY-VL53L0XV2 Laser Ranger Module: The GY-VL53L0XV2 is based on the VL53L0X from ST Microelectronics, a time-of-flight ranging system integrated into a compact module.
